# Fritzing sketch cabling (saved by Fritzing 0.9.3b)
breadboards: 1

parts:
  Composant1 = Thumb Joystick
  Composant2 = Arduino Nano (Rev3.0)
  J1 = Basic Servo

nets:
  GND: Composant1.GND, Composant2.GND, J1.gnd
  N1: Composant1.HORZ, Composant2.A0
  VCC: Composant1.VCC, Composant2.5V, J1.vcc
  N2: Composant2.D3, J1.pulse
